# Fritzing sketch barra (saved by Fritzing 0.8.7b)

parts:
  Componente1 = Arduino Uno (Rev3) - ICSP
  U1 = 74HC595 [package="DIP16 [THT]"]
  R2 = Resistor [tolerance=±5% resistance=330 package=THT]
  R3 = Resistor [tolerance=±5% resistance=330 package=THT]
  R4 = Resistor [tolerance=±5% resistance=330 package=THT]
  R5 = Resistor [tolerance=±5% resistance=330 package=THT]
  R6 = Resistor [tolerance=±5% resistance=330 package=THT]
  R7 = Resistor [tolerance=±5% resistance=330 package=THT]
  R8 = Resistor [tolerance=±5% resistance=330 package=THT]
  R9 = Resistor [tolerance=±5% resistance=330 package=THT]
  R10 = Resistor [tolerance=±5% resistance=330 package=THT]
  R11 = Resistor [tolerance=±5% resistance=330 package=THT]
  D1 = LED_BARGRAPH_10 [part_number=B210SR package=led_bargaph_10]
  U2 = POT [package=pot_alpha_rv16af-20]
  R12 = Resistor [tolerance=±5% resistance=330 package=THT]
  R13 = Resistor [tolerance=±5% resistance=330 package=THT]
  R14 = Resistor [tolerance=±5% resistance=330 package=THT]
  R15 = Resistor [tolerance=±5% resistance=220 package=THT]

nets:
  N1: Componente1.A0, U2.S
  5V: Componente1.5V, U1.VCC, U2.E, R12.Pin_1, R13.Pin_1, R15.Pin_1
  GND: Componente1.GND, U1.GND, U1.OE, D1.J_C, D1.I_C, D1.H_C, D1.G_C, D1.F_C, D1.E_C, D1.D_C, D1.C_C, D1.B_C, D1.A_C, U2.A
  N2: Componente1.D2, R10.Pin_0
  N3: Componente1.D3_PWM, R11.Pin_0
  N4: Componente1.D4, R14.Pin_0
  N5: U1.Q1, R3.Pin_0
  N6: U1.Q2, R4.Pin_0
  N7: U1.Q3, R5.Pin_0
  N8: U1.Q4, R6.Pin_0
  N9: U1.Q5, R7.Pin_0
  N10: U1.Q6, R8.Pin_0
  N11: U1.Q7, R9.Pin_0
  N12: U1.MR, R15.Pin_0
  N13: U1.SH_CP, R14.Pin_1
  N14: U1.ST_CP, R11.Pin_1
  N15: U1.DS, R10.Pin_1
  N16: U1.Q0, R2.Pin_1
  N17: R2.Pin_0, D1.C_A
  N18: R3.Pin_1, D1.D_A
  N19: R4.Pin_1, D1.E_A
  N20: R5.Pin_1, D1.F_A
  N21: R6.Pin_1, D1.G_A
  N22: R7.Pin_1, D1.H_A
  N23: R8.Pin_1, D1.I_A
  N24: R9.Pin_1, D1.J_A
  N25: D1.A_A, R12.Pin_0
  N26: D1.B_A, R13.Pin_0
