# Fritzing sketch shifter (saved by Fritzing 0.8.7b)

parts:
  Componente1 = Arduino Uno (Rev3) - ICSP
  U1 = 74HC595 [package="DIP16 [THT]"]
  R1 = Resistor [tolerance=±5% resistance=220 package=THT]
  LED1 = LED - 5mm [color="Red (633nm)" package="5 mm [THT]"]
  LED2 = LED - 5mm [color="Red (633nm)" package="5 mm [THT]"]
  LED3 = LED - 5mm [color="Red (633nm)" package="5 mm [THT]"]
  LED4 = LED - 5mm [color="Red (633nm)" package="5 mm [THT]"]
  LED5 = LED - 5mm [color="Red (633nm)" package="5 mm [THT]"]
  LED6 = LED - 5mm [color="Red (633nm)" package="5 mm [THT]"]
  LED7 = LED - 5mm [color="Red (633nm)" package="5 mm [THT]"]
  LED8 = LED - 5mm [color="Red (633nm)" package="5 mm [THT]"]
  R2 = Resistor [tolerance=±5% resistance=330 package=THT]
  R3 = Resistor [tolerance=±5% resistance=330 package=THT]
  R4 = Resistor [tolerance=±5% resistance=330 package=THT]
  R5 = Resistor [tolerance=±5% resistance=330 package=THT]
  R6 = Resistor [tolerance=±5% resistance=330 package=THT]
  R7 = Resistor [tolerance=±5% resistance=330 package=THT]
  R8 = Resistor [tolerance=±5% resistance=330 package=THT]
  R9 = Resistor [tolerance=±5% resistance=330 package=THT]
  R10 = Resistor [tolerance=±5% resistance=330 package=THT]
  R11 = Resistor [tolerance=±5% resistance=330 package=THT]

nets:
  GND: Componente1.GND, U1.GND, U1.OE, LED1.cathode, LED2.cathode, LED3.cathode, LED4.cathode, LED5.cathode, LED6.cathode, LED7.cathode, LED8.cathode
  N1: Componente1.D2, R10.Pin_0
  N2: Componente1.D3_PWM, R11.Pin_0
  N3: Componente1.D4, U1.SH_CP
  5V: Componente1.5V, U1.VCC, R1.Pin_1
  N4: U1.Q1, R3.Pin_0
  N5: U1.Q2, R4.Pin_0
  N6: U1.Q3, R5.Pin_0
  N7: U1.Q4, R6.Pin_0
  N8: U1.Q5, R7.Pin_0
  N9: U1.Q6, R8.Pin_0
  N10: U1.Q7, R9.Pin_0
  N11: U1.MR, R1.Pin_0
  N12: U1.ST_CP, R11.Pin_1
  N13: U1.DS, R10.Pin_1
  N14: U1.Q0, R2.Pin_1
  N15: LED1.anode, R2.Pin_0
  N16: LED2.anode, R3.Pin_1
  N17: LED3.anode, R4.Pin_1
  N18: LED4.anode, R5.Pin_1
  N19: LED5.anode, R6.Pin_1
  N20: LED6.anode, R7.Pin_1
  N21: LED7.anode, R8.Pin_1
  N22: LED8.anode, R9.Pin_1
